// Logisim project Fumeirao_substituicoes_corrigidas.circ as structural Verilog
module Jogadores (
);

  wire B_GD, B_GE, BD1, BD2, BD3, BD4, BD5, BD6, BD7, BD8, BD9, BD10, BE1, BE2, BE3, BE4, BE5, BE6, BE7, BE8,
       BE9, BE10, CLK, D1, D2, D3, D4, D5, D6, D7, D8, D9, D10, E1, E2, E3, E4, E5, E6, E7, E8, E9, E10, GOL,
       M, or_1_out, or_2_out, or_3_out, or_4_out, or_5_out, or_6_out, or_7_out, or_8_out, or_9_out,
       or_10_out, or_11_out, or_12_out, or_13_out;

  Button Jog_1__E1 (.out(BE1));
  Button Jog_2__E2 (.out(BE2));
  Button Jog_3__E3 (.out(BE3));
  Button Jog_4__E4 (.out(BE4));
  Button Jog_5__E5 (.out(BE5));
  Button Jog_6__E6 (.out(BE6));
  Button Jog_7__E7 (.out(BE7));
  Button Atacante_8__E8 (.out(BE8));
  Button Atacante_9__E9 (.out(BE9));
  Button Atacante_10__E10 (.out(BE10));
  Button u_GOL (.out(B_GE));
  or or_1 (or_1_out, E8, E9, E10, D9, D10);
  or or_2 (or_2_out, B_GE, B_GD);
  or or_3 (or_3_out, E1, E2, E3, E4, E5);
  or or_4 (or_4_out, E6, E7, E8, E9, E10);
  or or_5 (or_5_out, D1, D2, D3, D4, D5);
  or or_6 (or_6_out, D6, D7, D8, D9, D10);
  and and_1 (GOL, or_1_out, or_2_out);
  or or_7 (or_7_out, or_3_out, or_4_out);
  or or_8 (or_8_out, or_5_out, or_6_out);
  LED led_1 (.in(1'b1));
  LED led_2 (.in(E5));
  LED led_3 (.in(E7));
  D_Flip_Flop FF_E1 (.clk(CLK), .D(BE1), .Q(E1));  // open: Qn, preset, en, reset
  D_Flip_Flop FF_E2 (.clk(CLK), .D(BE2), .Q(E2));  // open: Qn, preset, en, reset
  D_Flip_Flop FF_E3 (.clk(CLK), .D(BE3), .Q(E3));  // open: Qn, preset, en, reset
  D_Flip_Flop FF_E4 (.clk(CLK), .D(BE4), .Q(E4));  // open: Qn, preset, en, reset
  D_Flip_Flop FF_E5 (.clk(CLK), .D(BE5), .Q(E5));  // open: Qn, preset, en, reset
  or or_9 (or_9_out, or_7_out, or_8_out);
  LED led_4 (.in(E1));
  LED led_5 (.in(E2));
  LED led_6 (.in(E3));
  LED led_7 (.in(D9));
  LED led_8 (.in(E6));
  LED led_9 (.in(D10));
  not not_1 (M, or_9_out);
  LED led_10 (.in(D1));
  LED led_11 (.in(D4));
  LED led_12 (.in(E4));
  LED led_13 (.in(D8));
  D_Flip_Flop FF_E6 (.clk(CLK), .D(BE6), .Q(E6));  // open: Qn, preset, en, reset
  D_Flip_Flop FF_E7 (.clk(CLK), .D(BE7), .Q(E7));  // open: Qn, preset, en, reset
  D_Flip_Flop FF_E8 (.clk(CLK), .D(BE8), .Q(E8));  // open: Qn, preset, en, reset
  D_Flip_Flop FF_E9 (.clk(CLK), .D(BE9), .Q(E9));  // open: Qn, preset, en, reset
  D_Flip_Flop FF_E10 (.clk(CLK), .D(BE10), .Q(E10));  // open: Qn, preset, en, reset
  or or_10 (or_10_out, BE1, BE2, BE3, BE4, BE5);
  or or_11 (or_11_out, BE6, BE7, BE8, BE9, BE10);
  or or_12 (or_12_out, BD1, BD2, BD3, BD4, BD5);
  or or_13 (or_13_out, BD6, BD7, BD8, BD9, BD10);
  LED led_14 (.in(D3));
  LED led_15 (.in(M));
  LED led_16 (.in(D6));
  LED led_17 (.in(E8));
  LED led_18 (.in(E9));
  LED led_19 (.in(E10));
  D_Flip_Flop FF_D1 (.clk(CLK), .D(BD1), .Q(D1));  // open: Qn, preset, en, reset
  D_Flip_Flop FF_D2 (.clk(CLK), .D(BD2), .Q(D2));  // open: Qn, preset, en, reset
  D_Flip_Flop FF_D3 (.clk(CLK), .D(BD3), .Q(D3));  // open: Qn, preset, en, reset
  D_Flip_Flop FF_D4 (.clk(CLK), .D(BD4), .Q(D4));  // open: Qn, preset, en, reset
  D_Flip_Flop FF_D5 (.clk(CLK), .D(BD5), .Q(D5));  // open: Qn, preset, en, reset
  or or_14 (CLK, or_10_out, or_11_out, GOL, or_12_out, or_13_out);
  LED led_20 (.in(D2));
  LED led_21 (.in(D5));
  LED led_22 (.in(D7));
  LED led_23 (.in(1'b1));
  D_Flip_Flop FF_D6 (.clk(CLK), .D(BD6), .Q(D6));  // open: Qn, preset, en, reset
  D_Flip_Flop FF_D7 (.clk(CLK), .D(BD7), .Q(D7));  // open: Qn, preset, en, reset
  D_Flip_Flop FF_D8 (.clk(CLK), .D(BD8), .Q(D8));  // open: Qn, preset, en, reset
  D_Flip_Flop FF_D9 (.clk(CLK), .D(BD9), .Q(D9));  // open: Qn, preset, en, reset
  D_Flip_Flop FF_D10 (.clk(CLK), .D(BD10), .Q(D10));  // open: Qn, preset, en, reset
  Button Jog_1__D1 (.out(BD1));
  Button Jog_2__D2 (.out(BD2));
  Button Jog_3__D3 (.out(BD3));
  Button Jog_4__D4 (.out(BD4));
  Button Jog_5__D5 (.out(BD5));
  Button Jog_6__D6 (.out(BD6));
  Button Jog_7__D7 (.out(BD7));
  Button Jog_8__D8 (.out(BD8));
  Button Atacante_9__D9 (.out(BD9));
  Button Atacante_10__D10 (.out(BD10));
  Button GOL_2 (.out(B_GD));

  // Notes on the sheet:
  //   Time Esquerda
  //   VALIDADOR DE GOL
  //   CONTROLE DO LED AMARELO CENTRAL
  //   GERADOR DE PULSO DE ATUALIZAÇÃO
  //   CIRCUITO DE CONTROLE DE POSSE DE BOLA E VALIDACAO DE GOL
  //   Time Direita
endmodule

module Placar (
);

  wire desempate_1_empate, desempate_1_fim_partida, desempate_1_prorrogacao, GOL_A, GOL_V, LIMPA_PLACAR_90,
       RST_A, RST_V, TRAVA_PLACAR_90, Uni_ASA_carry, Uni_Vis_carry;
  wire [3:0] QA_D, QA_U, QV_D, QV_U;

  Button Gol_ASA (.out(GOL_A));
  Button reset_ASA (.out(RST_A));
  Counter #(.width(4), .max('h9)) Uni_ASA (
    .count(GOL_A), .Q(QA_U), .carry(Uni_ASA_carry), .clk(GOL_A), .clr(RST_A));  // open: load, D
  Counter #(.width(4), .max('h9)) Dez_ASA (
    .count(Uni_ASA_carry), .Q(QA_D), .clk(GOL_A), .clr(RST_A));  // open: load, D, carry
  Button VALIDAR_90_MIN (.out(TRAVA_PLACAR_90));
  Button REINICIAR_DESEMPATE (.out(LIMPA_PLACAR_90));
  Hex_Digit_Display hex_digit_display_1 (.value(QA_D));  // open: dp
  Hex_Digit_Display hex_digit_display_2 (.value(QA_U));  // open: dp
  Hex_Digit_Display hex_digit_display_3 (.value(QV_U));  // open: dp
  Hex_Digit_Display hex_digit_display_4 (.value(QV_D));  // open: dp
  Desempate desempate_1 (
    .ASA_DEZ(QA_D), .ASA_UNI(QA_U), .VIS_DEZ(QV_D), .VIS_UNI(QV_U), .VALIDAR_90(TRAVA_PLACAR_90),
    .REINICIAR(LIMPA_PLACAR_90), .EMPATE(desempate_1_empate), .PRORROGACAO(desempate_1_prorrogacao),
    .FIM_PARTIDA(desempate_1_fim_partida));
  Counter #(.width(4), .max('h9)) Uni_Vis (
    .count(GOL_V), .Q(QV_U), .carry(Uni_Vis_carry), .clk(GOL_V), .clr(RST_V));  // open: load, D
  LED EMPATE_AGORA (.in(desempate_1_empate));
  LED PRORROGACAO (.in(desempate_1_prorrogacao));
  LED PARTIDA_ENCERRADA (.in(desempate_1_fim_partida));
  Counter #(.width(4), .max('h9)) Dez_Vis (
    .count(Uni_Vis_carry), .Q(QV_D), .clk(GOL_V), .clr(RST_V));  // open: load, D, carry
  Button Gol_Visitante (.out(GOL_V));
  Button reset_Visitante (.out(RST_V));
endmodule

module Cronometro (
  input  Run
);

  wire and_3_out, C_DS, C_US, CLK_RUN, clock_1_out, De_Seg_carry, RST, Uni_min_carry;
  wire [3:0] DM, DS, UM, US;

  Clock clock_1 (.out(clock_1_out));
  Button Reset (.out(RST));
  and and_1 (CLK_RUN, Run, clock_1_out);
  Hex_Digit_Display hex_digit_display_1 (.value(UM));  // open: dp
  Hex_Digit_Display hex_digit_display_2 (.value(DM));  // open: dp
  Counter #(.width(4), .max('h9)) Uni_seg (
    .count(CLK_RUN), .Q(US), .carry(C_US), .clk(CLK_RUN), .clr(RST));  // open: load, D
  Hex_Digit_Display hex_digit_display_3 (.value(DS));  // open: dp
  Counter #(.width(4), .max('h5)) De_Seg (
    .count(C_US), .Q(DS), .carry(De_Seg_carry), .clk(CLK_RUN), .clr(RST));  // open: load, D
  Hex_Digit_Display hex_digit_display_4 (.value(US));  // open: dp
  and and_2 (C_DS, De_Seg_carry, C_US);
  Counter #(.width(4), .max('h9)) Uni_min (
    .count(C_DS), .Q(UM), .carry(Uni_min_carry), .clk(CLK_RUN), .clr(RST));  // open: load, D
  and and_3 (and_3_out, Uni_min_carry, C_DS);
  Counter #(.width(4), .max('h9)) De_min (.count(and_3_out), .Q(DM), .clk(CLK_RUN), .clr(RST));  // open: load, D, carry
endmodule

module Desempate (
  input  [3:0] ASA_DEZ,
  input  [3:0] ASA_UNI,
  input  [3:0] VIS_DEZ,
  input  [3:0] VIS_UNI,
  input  VALIDAR_90,
  input  REINICIAR,
  output EMPATE,
  output PRORROGACAO,
  output FIM_PARTIDA
);

  wire comparator_1_eq, comparator_2_eq, not_1_out;

  Comparator #(.width(4), .mode("unsigned")) comparator_1 (
    .a(ASA_DEZ), .b(VIS_DEZ), .eq(comparator_1_eq));  // open: gt, lt
  Comparator #(.width(4), .mode("unsigned")) comparator_2 (
    .a(ASA_UNI), .b(VIS_UNI), .eq(comparator_2_eq));  // open: gt, lt
  and and_1 (EMPATE, comparator_1_eq, comparator_2_eq);
  not not_1 (not_1_out, EMPATE);
  Register #(.width(1)) u_PRORROGACAO (.D(EMPATE), .en(1'b1), .Q(PRORROGACAO), .clk(VALIDAR_90), .clr(REINICIAR));
  Register #(.width(1)) ENCERRADA (.D(not_1_out), .en(1'b1), .Q(FIM_PARTIDA), .clk(VALIDAR_90), .clr(REINICIAR));

  // Other names for the same wires on the sheet: IGUAL = EMPATE; LIMPA_90 = REINICIAR; TRAVA_90 = VALIDAR_90
endmodule

module Motor_Subs_Minimo (
  input  EQUIPE,
  input  [3:0] SAI,
  input  [3:0] BANCO,
  input  [3:0] ENTRA,
  input  CONFIRMAR,
  input  RESET,
  output [3:0] ASA_N,
  output [3:0] AMADORES_N,
  output [3:0] ULT_SAI,
  output [3:0] ULT_BANCO,
  output [3:0] ULT_ENTRA,
  output ULT_EQ
);

  wire AMADORES_CONF, AMADORES_VAGA, ASA_CONF, ASA_VAGA, BANCO_E_POVO, BANCO_LT3, BASE_OK, DADOS_OK,
       ENTRA_GT0, ENTRA_LT12, ENTRA_OK, NOMES_OK, OUTRO_BANCO, PARCIAL_OK, PED_AMADORES, PED_ASA, PEDIDO,
       POSICAO_OK, RESERVA_OK, SAI_GT0, SAI_LT12, SAI_OK, TIME_ASA, TROCA_VALIDA;

  Comparator #(.width(4), .mode("unsigned")) comparator_1 (.a(SAI), .b(4'b0000), .gt(SAI_GT0));  // open: eq, lt
  Comparator #(.width(4), .mode("unsigned")) comparator_2 (.a(SAI), .b(4'b1100), .lt(SAI_LT12));  // open: gt, eq
  Comparator #(.width(4), .mode("unsigned")) comparator_3 (.a(ENTRA), .b(4'b0000), .gt(ENTRA_GT0));  // open: eq, lt
  Comparator #(.width(4), .mode("unsigned")) comparator_4 (.a(ENTRA), .b(4'b1100), .lt(ENTRA_LT12));  // open: gt, eq
  Comparator #(.width(4), .mode("unsigned")) comparator_5 (.a(BANCO), .b(4'b0011), .lt(BANCO_LT3));  // open: gt, eq
  Comparator #(.width(4), .mode("unsigned")) comparator_6 (.a(SAI), .b(4'b1100), .lt(SAI_LT12));  // open: gt, eq
  Comparator #(.width(4), .mode("unsigned")) comparator_7 (.a(ENTRA), .b(4'b1100), .lt(ENTRA_LT12));  // open: gt, eq
  Comparator #(.width(4), .mode("unsigned")) comparator_8 (.a(BANCO), .b(4'b0001), .eq(BANCO_E_POVO));  // open: gt, lt
  not not_1 (OUTRO_BANCO, BANCO_E_POVO);
  and and_1 (SAI_OK, SAI_GT0, SAI_LT12);
  and and_2 (ENTRA_OK, ENTRA_GT0, ENTRA_LT12);
  or or_1 (POSICAO_OK, EQUIPE, SAI_LT12);
  not not_2 (TIME_ASA, EQUIPE);
  and and_3 (NOMES_OK, SAI_OK, ENTRA_OK);
  or or_2 (RESERVA_OK, OUTRO_BANCO, ENTRA_LT12);
  and and_4 (PED_ASA, PEDIDO, TIME_ASA);
  and and_5 (PED_AMADORES, PEDIDO, EQUIPE);
  and and_6 (BASE_OK, NOMES_OK, BANCO_LT3);
  // Counter #(.width(4), .max('hf), .ongoal("stay")) TOTAL_ASA: pin names not known; wires that end beside it: 1'b1, 1'b0, ASA_CONF, ASA_N
  // Counter #(.width(4), .max('hf), .ongoal("stay")) TOTAL_AMADORES: pin names not known; wires that end beside it: 1'b1, 1'b0, AMADORES_CONF, AMADORES_N
  and and_7 (ASA_CONF, PED_ASA, ASA_VAGA);
  and and_8 (AMADORES_CONF, PED_AMADORES, AMADORES_VAGA);
  and and_9 (PARCIAL_OK, BASE_OK, POSICAO_OK);
  or or_3 (TROCA_VALIDA, ASA_CONF, AMADORES_CONF);
  Register #(.width(4)) u_ULT_SAI (.D(SAI), .en(1'b1), .Q(ULT_SAI), .clk(TROCA_VALIDA));  // open: clr
  Register #(.width(4)) u_ULT_BANCO (.D(BANCO), .en(1'b1), .Q(ULT_BANCO), .clk(TROCA_VALIDA));  // open: clr
  Register #(.width(4)) u_ULT_ENTRA (.D(ENTRA), .en(1'b1), .Q(ULT_ENTRA), .clk(TROCA_VALIDA));  // open: clr
  Register #(.width(1)) ULT_EQUIPE (.D(EQUIPE), .en(1'b1), .Q(ULT_EQ), .clk(TROCA_VALIDA));  // open: clr
  and and_10 (DADOS_OK, PARCIAL_OK, RESERVA_OK);
  Comparator #(.width(4), .mode("unsigned")) comparator_9 (.a(ASA_N), .b(4'b0101), .lt(ASA_VAGA));  // open: gt, eq
  Comparator #(.width(4), .mode("unsigned")) comparator_10 (
    .a(AMADORES_N), .b(4'b0101), .lt(AMADORES_VAGA));  // open: gt, eq
  and and_11 (PEDIDO, CONFIRMAR, DADOS_OK);

  // Other names for the same wires on the sheet: COUNT_AMADORES[3:0] = AMADORES_N; OUT_AMADORES_N[3:0] = AMADORES_N;
  //   COUNT_ASA[3:0] = ASA_N; OUT_ASA_N[3:0] = ASA_N; LAST_BANCO[3:0] = ULT_BANCO; OUT_ULT_BANCO[3:0] = ULT_BANCO;
  //   LAST_ENTRA[3:0] = ULT_ENTRA; OUT_ULT_ENTRA[3:0] = ULT_ENTRA; LAST_EQUIPE = ULT_EQ; OUT_ULT_EQ = ULT_EQ;
  //   LAST_SAI[3:0] = ULT_SAI; OUT_ULT_SAI[3:0] = ULT_SAI
endmodule

module \Substituição  (
  input  EQUIPE,
  input  [3:0] SAI,
  input  [3:0] BANCO,
  input  [3:0] ENTRA
);

  wire CONFIRMAR, RES_ULT_EQ, RESET;
  wire [3:0] RES_AMADORES_N, RES_ASA_N, RES_ULT_BANCO, RES_ULT_ENTRA, RES_ULT_SAI;

  Hex_Digit_Display hex_digit_display_1 (.value(RES_ASA_N));  // open: dp
  Hex_Digit_Display hex_digit_display_2 (.value(RES_AMADORES_N));  // open: dp
  Hex_Digit_Display hex_digit_display_3 (.value(RES_ULT_SAI));  // open: dp
  Button u_CONFIRMAR (.out(CONFIRMAR));
  Hex_Digit_Display hex_digit_display_4 (.value(RES_ULT_BANCO));  // open: dp
  Painel_3_Listas painel_3_listas_1 ();
  Button u_RESET (.out(RESET));
  Hex_Digit_Display hex_digit_display_5 (.value(RES_ULT_ENTRA));  // open: dp
  LED ULT_AMADORES (.in(RES_ULT_EQ));
  Motor_Subs_Minimo motor_subs_minimo_1 (
    .RESET(RESET), .CONFIRMAR(CONFIRMAR), .ENTRA(ENTRA), .BANCO(BANCO), .SAI(SAI), .EQUIPE(EQUIPE),
    .ASA_N(RES_ASA_N), .AMADORES_N(RES_AMADORES_N), .ULT_SAI(RES_ULT_SAI), .ULT_BANCO(RES_ULT_BANCO),
    .ULT_ENTRA(RES_ULT_ENTRA), .ULT_EQ(RES_ULT_EQ));

  // Notes on the sheet:
  //   0 ASA / 1 AMADORES
  //   ASA / 5
  //   SAI 1-11
  //   AMADORES / 5
  //   0 Lendas / 1 Povo / 2 Amadores
  //   SAI
  //   BANCO
  //   ENTRA
endmodule
