// Logisim project Fumeirão.circ as structural Verilog
module Jogadores_Circuito (
);

  wire B_GD, B_GE, BD1, BD2, BD3, BD4, BD5, BD6, BD7, BD8, BD9, BD10, BE1, BE2, BE3, BE4, BE5, BE6, BE7, BE8,
       BE9, BE10, CLK, D1, D2, D3, D4, D5, D6, D7, D8, D9, D10, E1, E2, E3, E4, E5, E6, E7, E8, E9, E10, GOL,
       M, or_1_out, or_2_out, or_3_out, or_4_out, or_5_out, or_6_out, or_7_out, or_8_out, or_9_out,
       or_10_out, or_11_out, or_12_out, or_13_out;

  Button Jog_1__E1 (.out(BE1));
  Button Jog_2__E2 (.out(BE2));
  Button Jog_3__E3 (.out(BE3));
  Button Jog_4__E4 (.out(BE4));
  Button Jog_5__E5 (.out(BE5));
  Button Jog_6__E6 (.out(BE6));
  Button Jog_7__E7 (.out(BE7));
  Button Atacante_8__E8 (.out(BE8));
  Button Atacante_9__E9 (.out(BE9));
  Button Atacante_10__E10 (.out(BE10));
  Button u_GOL (.out(B_GE));
  or or_1 (or_1_out, E8, E9, E10, D9, D10);
  or or_2 (or_2_out, B_GE, B_GD);
  or or_3 (or_3_out, E1, E2, E3, E4, E5);
  or or_4 (or_4_out, E6, E7, E8, E9, E10);
  or or_5 (or_5_out, D1, D2, D3, D4, D5);
  or or_6 (or_6_out, D6, D7, D8, D9, D10);
  and and_1 (GOL, or_1_out, or_2_out);
  or or_7 (or_7_out, or_3_out, or_4_out);
  or or_8 (or_8_out, or_5_out, or_6_out);
  LED led_1 (.in(1'b1));
  LED led_2 (.in(E5));
  LED led_3 (.in(E7));
  D_Flip_Flop FF_E1 (.clk(CLK), .D(BE1), .Q(E1));  // open: Qn, preset, en, reset
  D_Flip_Flop FF_E2 (.clk(CLK), .D(BE2), .Q(E2));  // open: Qn, preset, en, reset
  D_Flip_Flop FF_E3 (.clk(CLK), .D(BE3), .Q(E3));  // open: Qn, preset, en, reset
  D_Flip_Flop FF_E4 (.clk(CLK), .D(BE4), .Q(E4));  // open: Qn, preset, en, reset
  D_Flip_Flop FF_E5 (.clk(CLK), .D(BE5), .Q(E5));  // open: Qn, preset, en, reset
  or or_9 (or_9_out, or_7_out, or_8_out);
  LED led_4 (.in(E1));
  LED led_5 (.in(E2));
  LED led_6 (.in(E3));
  LED led_7 (.in(D9));
  LED led_8 (.in(E6));
  LED led_9 (.in(D10));
  not not_1 (M, or_9_out);
  LED led_10 (.in(D1));
  LED led_11 (.in(D4));
  LED led_12 (.in(E4));
  LED led_13 (.in(D8));
  D_Flip_Flop FF_E6 (.clk(CLK), .D(BE6), .Q(E6));  // open: Qn, preset, en, reset
  D_Flip_Flop FF_E7 (.clk(CLK), .D(BE7), .Q(E7));  // open: Qn, preset, en, reset
  D_Flip_Flop FF_E8 (.clk(CLK), .D(BE8), .Q(E8));  // open: Qn, preset, en, reset
  D_Flip_Flop FF_E9 (.clk(CLK), .D(BE9), .Q(E9));  // open: Qn, preset, en, reset
  D_Flip_Flop FF_E10 (.clk(CLK), .D(BE10), .Q(E10));  // open: Qn, preset, en, reset
  or or_10 (or_10_out, BE1, BE2, BE3, BE4, BE5);
  or or_11 (or_11_out, BE6, BE7, BE8, BE9, BE10);
  or or_12 (or_12_out, BD1, BD2, BD3, BD4, BD5);
  or or_13 (or_13_out, BD6, BD7, BD8, BD9, BD10);
  LED led_14 (.in(D3));
  LED led_15 (.in(M));
  LED led_16 (.in(D6));
  LED led_17 (.in(E8));
  LED led_18 (.in(E9));
  LED led_19 (.in(E10));
  D_Flip_Flop FF_D1 (.clk(CLK), .D(BD1), .Q(D1));  // open: Qn, preset, en, reset
  D_Flip_Flop FF_D2 (.clk(CLK), .D(BD2), .Q(D2));  // open: Qn, preset, en, reset
  D_Flip_Flop FF_D3 (.clk(CLK), .D(BD3), .Q(D3));  // open: Qn, preset, en, reset
  D_Flip_Flop FF_D4 (.clk(CLK), .D(BD4), .Q(D4));  // open: Qn, preset, en, reset
  D_Flip_Flop FF_D5 (.clk(CLK), .D(BD5), .Q(D5));  // open: Qn, preset, en, reset
  or or_14 (CLK, or_10_out, or_11_out, GOL, or_12_out, or_13_out);
  LED led_20 (.in(D2));
  LED led_21 (.in(D5));
  LED led_22 (.in(D7));
  LED led_23 (.in(1'b1));
  D_Flip_Flop FF_D6 (.clk(CLK), .D(BD6), .Q(D6));  // open: Qn, preset, en, reset
  D_Flip_Flop FF_D7 (.clk(CLK), .D(BD7), .Q(D7));  // open: Qn, preset, en, reset
  D_Flip_Flop FF_D8 (.clk(CLK), .D(BD8), .Q(D8));  // open: Qn, preset, en, reset
  D_Flip_Flop FF_D9 (.clk(CLK), .D(BD9), .Q(D9));  // open: Qn, preset, en, reset
  D_Flip_Flop FF_D10 (.clk(CLK), .D(BD10), .Q(D10));  // open: Qn, preset, en, reset
  Button Jog_1__D1 (.out(BD1));
  Button Jog_2__D2 (.out(BD2));
  Button Jog_3__D3 (.out(BD3));
  Button Jog_4__D4 (.out(BD4));
  Button Jog_5__D5 (.out(BD5));
  Button Jog_6__D6 (.out(BD6));
  Button Jog_7__D7 (.out(BD7));
  Button Jog_8__D8 (.out(BD8));
  Button Atacante_9__D9 (.out(BD9));
  Button Atacante_10__D10 (.out(BD10));
  Button GOL_2 (.out(B_GD));

  // Notes on the sheet:
  //   Time Esquerda
  //   VALIDADOR DE GOL
  //   CONTROLE DO LED AMARELO CENTRAL
  //   GERADOR DE PULSO DE ATUALIZAÇÃO
  //   CIRCUITO DE CONTROLE DE POSSE DE BOLA E VALIDACAO DE GOL
  //   Time Direita
endmodule

module Placar (
  input  Run
);

  wire and_5_out, and_6_out, and_9_out, and_13_out, ASA_GT_VIS, BTN_GOL_A, BTN_VAL, C_DM, C_DS, C_UM, C_US,
       CLK_CRON, CLK_VAL, CM_0, CM_1, D_EQ, D_GT, De_min_carry, De_Seg_carry, DM_2, DM_9, DS_0, ENC, FIM,
       GOL_A, GOL_V, IGUAL, N_ENC, N_IGUAL, N_PRORR, not_4_out, not_5_out, or_2_out, or_5_out, PAUSA_90,
       PAUSA_120, PAUSA_TEMPO, PRORR, RST_A, RST_ALL, RST_CRON, RST_DES, RST_V, SYS_CLK, T90, T120, U_EQ,
       U_GT, UM_0, Uni_ASA_carry, Uni_min_carry, Uni_Vis_carry, US_0;
  wire [3:0] CM, DM, DS, QA_D, QA_U, QV_D, QV_U, UM, US;

  Button Gol_ASA (.out(BTN_GOL_A));
  Button reset_ASA (.out(RST_A));
  Clock Clock_Jogo (.out(SYS_CLK));
  Button Reset_Cronometro (.out(RST_CRON));
  Comparator #(.width(4), .mode("unsigned")) comparator_1 (.a(UM), .b(4'b0000), .eq(UM_0));  // open: gt, lt
  Comparator #(.width(4), .mode("unsigned")) comparator_2 (.a(DS), .b(4'b0000), .eq(DS_0));  // open: gt, lt
  Comparator #(.width(4), .mode("unsigned")) comparator_3 (.a(US), .b(4'b0000), .eq(US_0));  // open: gt, lt
  Comparator #(.width(4), .mode("unsigned")) comparator_4 (.a(CM), .b(4'b0000), .eq(CM_0));  // open: gt, lt
  Comparator #(.width(4), .mode("unsigned")) comparator_5 (.a(DM), .b(4'b1001), .eq(DM_9));  // open: gt, lt
  Comparator #(.width(4), .mode("unsigned")) comparator_6 (.a(CM), .b(4'b0001), .eq(CM_1));  // open: gt, lt
  Comparator #(.width(4), .mode("unsigned")) comparator_7 (.a(DM), .b(4'b0010), .eq(DM_2));  // open: gt, lt
  Counter #(.width(4), .max('h9)) Uni_ASA (
    .count(GOL_A), .Q(QA_U), .carry(Uni_ASA_carry), .clk(GOL_A), .clr(RST_A));  // open: load, D
  Counter #(.width(4), .max('h9)) Uni_seg (
    .count(CLK_CRON), .Q(US), .carry(C_US), .clk(CLK_CRON), .clr(RST_CRON));  // open: load, D
  Counter #(.width(4), .max('h9)) Dez_ASA (
    .count(Uni_ASA_carry), .Q(QA_D), .clk(GOL_A), .clr(RST_A));  // open: load, D, carry
  Button VALIDAR_90_120_MIN (.out(BTN_VAL));
  Button REINICIAR_DESEMPATE (.out(RST_DES));
  and and_1 (T90, CM_0, DM_9, UM_0, DS_0, US_0);
  and and_2 (T120, CM_1, DM_2, UM_0, DS_0, US_0);
  or or_1 (RST_ALL, RST_DES, RST_CRON);
  and and_3 (CLK_VAL, BTN_VAL, PAUSA_TEMPO);
  Hex_Digit_Display hex_digit_display_1 (.value(CM));  // open: dp
  Hex_Digit_Display hex_digit_display_2 (.value(DM));  // open: dp
  Counter #(.width(4), .max('h5)) De_Seg (
    .count(C_US), .Q(DS), .carry(De_Seg_carry), .clk(CLK_CRON), .clr(RST_CRON));  // open: load, D
  Hex_Digit_Display hex_digit_display_3 (.value(QA_D));  // open: dp
  Hex_Digit_Display hex_digit_display_4 (.value(QA_U));  // open: dp
  Hex_Digit_Display hex_digit_display_5 (.value(UM));  // open: dp
  Hex_Digit_Display hex_digit_display_6 (.value(DS));  // open: dp
  and and_4 (C_DS, De_Seg_carry, C_US);
  Comparator #(.width(4), .mode("unsigned")) comparator_8 (.a(QA_D), .b(QV_D), .gt(D_GT), .eq(D_EQ));  // open: lt
  Comparator #(.width(4), .mode("unsigned")) comparator_9 (.a(QA_U), .b(QV_U), .gt(U_GT), .eq(U_EQ));  // open: lt
  not not_1 (N_PRORR, PRORR);
  not not_2 (N_ENC, ENC);
  not not_3 (N_IGUAL, IGUAL);
  and and_5 (and_5_out, T90, IGUAL);
  and and_6 (and_6_out, T90, N_IGUAL);
  Hex_Digit_Display hex_digit_display_7 (.value(US));  // open: dp
  Counter #(.width(4), .max('h9)) Uni_min (
    .count(C_DS), .Q(UM), .carry(Uni_min_carry), .clk(CLK_CRON), .clr(RST_CRON));  // open: load, D
  Hex_Digit_Display hex_digit_display_8 (.value(QV_D));  // open: dp
  Hex_Digit_Display hex_digit_display_9 (.value(QV_U));  // open: dp
  LED AGUARDANDO_VALIDACAO (.in(PAUSA_TEMPO));
  LED EMPATE_AGORA (.in(IGUAL));
  LED PRORROGACAO (.in(PRORR));
  LED PARTIDA_ENCERRADA (.in(FIM));
  Register #(.width(1)) REG_PRORR (.D(and_5_out), .en(1'b1), .Q(PRORR), .clk(CLK_VAL), .clr(RST_ALL));
  or or_2 (or_2_out, and_6_out, T120);
  and and_7 (C_UM, Uni_min_carry, C_DS);
  and and_8 (IGUAL, D_EQ, U_EQ);
  and and_9 (and_9_out, D_EQ, U_GT);
  and and_10 (PAUSA_90, T90, N_PRORR, N_ENC);
  and and_11 (PAUSA_120, T120, N_ENC);
  Register #(.width(1)) REG_ENC (.D(or_2_out), .en(1'b1), .Q(ENC), .clk(CLK_VAL), .clr(RST_ALL));
  Counter #(.width(4), .max('h9)) Uni_Vis (
    .count(GOL_V), .Q(QV_U), .carry(Uni_Vis_carry), .clk(GOL_V), .clr(RST_V));  // open: load, D
  or or_3 (ASA_GT_VIS, D_GT, and_9_out);
  Counter #(.width(4), .max('h9)) De_min (
    .count(C_UM), .Q(DM), .carry(De_min_carry), .clk(CLK_CRON), .clr(RST_CRON));  // open: load, D
  Counter #(.width(4), .max('h9)) Dez_Vis (
    .count(Uni_Vis_carry), .Q(QV_D), .clk(GOL_V), .clr(RST_V));  // open: load, D, carry
  or or_4 (PAUSA_TEMPO, PAUSA_90, PAUSA_120);
  or or_5 (or_5_out, PAUSA_TEMPO, ENC, FIM);
  not not_4 (not_4_out, ASA_GT_VIS);
  and and_12 (C_DM, De_min_carry, C_UM);
  not not_5 (not_5_out, or_5_out);
  and and_13 (and_13_out, ENC, not_4_out, SYS_CLK);
  and and_14 (FIM, ENC, ASA_GT_VIS);
  Counter #(.width(4), .max('h9)) Cen_min (
    .count(C_DM), .Q(CM), .clk(CLK_CRON), .clr(RST_CRON));  // open: load, D, carry
  Button Gol_Visitante (.out(GOL_V));
  Button reset_Visitante (.out(RST_V));
  and and_15 (CLK_CRON, Run, SYS_CLK, not_5_out);
  or or_6 (GOL_A, BTN_GOL_A, and_13_out);

  // Notes on the sheet:
  //   CRONOMETRO DE JOGO (000:00 ATE 090:00 E PRORROGACAO ATE 120:00)
  //   :
  //   PLACAR DO JOGO (MANDANTE ASA vs VISITANTE)
  //   X
  //   PAINEL DE DESEMPATE, PRORROGACAO E EFEITO GOL DO FANTASMA
  //   LOGICA DE DETECCAO DE 90/120 MIN, DESEMPATE E EFEITO GOL DO FANTASMA
endmodule

module \Substituição  (
  input  EQUIPE,
  input  [3:0] SAI,
  input  [3:0] BANCO,
  input  [3:0] ENTRA
);

  wire AMADORES_CONF, AMADORES_VAGA, and_1_out, ASA_CONF, ASA_VAGA, BANCO_LT3, comparator_6_eq, CONFIRMAR,
       DADOS_OK, DIF_OK, ENTRA_GT0, ENTRA_LT12, LAST_EQUIPE, PEDIDO, RESET, SAI_GT0, SAI_LT12, TIME_ASA,
       TROCA_VALIDA;
  wire [3:0] COUNT_AMADORES, COUNT_ASA, LAST_BANCO, LAST_ENTRA, LAST_SAI;

  Hex_Digit_Display hex_digit_display_1 (.value(COUNT_ASA));  // open: dp
  Hex_Digit_Display hex_digit_display_2 (.value(COUNT_AMADORES));  // open: dp
  Comparator #(.width(4), .mode("unsigned")) comparator_1 (.a(SAI), .b(4'b0000), .gt(SAI_GT0));  // open: eq, lt
  Comparator #(.width(4), .mode("unsigned")) comparator_2 (.a(SAI), .b(4'b1100), .lt(SAI_LT12));  // open: gt, eq
  Comparator #(.width(4), .mode("unsigned")) comparator_3 (.a(ENTRA), .b(4'b0000), .gt(ENTRA_GT0));  // open: eq, lt
  Comparator #(.width(4), .mode("unsigned")) comparator_4 (.a(ENTRA), .b(4'b1100), .lt(ENTRA_LT12));  // open: gt, eq
  Comparator #(.width(4), .mode("unsigned")) comparator_5 (.a(BANCO), .b(4'b0011), .lt(BANCO_LT3));  // open: gt, eq
  Comparator #(.width(4), .mode("unsigned")) comparator_6 (.a(SAI), .b(ENTRA), .eq(comparator_6_eq));  // open: gt, lt
  not not_1 (DIF_OK, comparator_6_eq);
  Hex_Digit_Display hex_digit_display_3 (.value(LAST_SAI));  // open: dp
  Button u_CONFIRMAR (.out(CONFIRMAR));
  Hex_Digit_Display hex_digit_display_4 (.value(LAST_BANCO));  // open: dp
  and and_1 (and_1_out, SAI_GT0, SAI_LT12, ENTRA_GT0, ENTRA_LT12, BANCO_LT3);
  and and_2 (PEDIDO, CONFIRMAR, DADOS_OK);
  not not_2 (TIME_ASA, EQUIPE);
  Jogadores_Tela jogadores_tela_1 ();
  Button u_RESET (.out(RESET));
  Hex_Digit_Display hex_digit_display_5 (.value(LAST_ENTRA));  // open: dp
  and and_3 (DADOS_OK, and_1_out, DIF_OK);
  and and_4 (ASA_CONF, PEDIDO, TIME_ASA, ASA_VAGA);
  and and_5 (AMADORES_CONF, PEDIDO, EQUIPE, AMADORES_VAGA);
  or or_1 (TROCA_VALIDA, ASA_CONF, AMADORES_CONF);
  LED ULT_AMADORES (.in(LAST_EQUIPE));
  Counter #(.width(4), .max('h5), .ongoal("stay")) TOTAL_ASA (
    .count(1'b1), .Q(COUNT_ASA), .clk(ASA_CONF), .clr(RESET));  // open: load, D, carry
  Counter #(.width(4), .max('h5), .ongoal("stay")) TOTAL_AMADORES (
    .count(1'b1), .Q(COUNT_AMADORES), .clk(AMADORES_CONF), .clr(RESET));  // open: load, D, carry
  Register #(.width(4)) ULT_SAI (.D(SAI), .en(1'b1), .Q(LAST_SAI), .clk(TROCA_VALIDA), .clr(RESET));
  Register #(.width(4)) ULT_BANCO (.D(BANCO), .en(1'b1), .Q(LAST_BANCO), .clk(TROCA_VALIDA), .clr(RESET));
  Register #(.width(4)) ULT_ENTRA (.D(ENTRA), .en(1'b1), .Q(LAST_ENTRA), .clk(TROCA_VALIDA), .clr(RESET));
  Register #(.width(1)) ULT_EQUIPE (.D(EQUIPE), .en(1'b1), .Q(LAST_EQUIPE), .clk(TROCA_VALIDA), .clr(RESET));
  Comparator #(.width(4), .mode("unsigned")) comparator_7 (.a(COUNT_ASA), .b(4'b0101), .lt(ASA_VAGA));  // open: gt, eq
  Comparator #(.width(4), .mode("unsigned")) comparator_8 (
    .a(COUNT_AMADORES), .b(4'b0101), .lt(AMADORES_VAGA));  // open: gt, eq

  // Notes on the sheet:
  //   0 ASA / 1 AMADORES
  //   ASA / 5
  //   SAI 1-11
  //   AMADORES / 5
  //   0 Lendas / 1 Povo / 2 Amadores
  //   SAI
  //   MOTOR DE VALIDACAO E CONTAGEM DE SUBSTITUICOES (CONDENSADO E CORRIGIDO)
  //   BANCO
  //   ENTRA
endmodule
