// Logisim project Placar_Cronometro.circ as structural Verilog
module Jogadores (
);

  wire B_GD, B_GE, BD1, BD2, BD3, BD4, BD5, BD6, BD7, BD8, BD9, BD10, BE1, BE2, BE3, BE4, BE5, BE6, BE7, BE8,
       BE9, BE10, CLK, D1, D2, D3, D4, D5, D6, D7, D8, D9, D10, E1, E2, E3, E4, E5, E6, E7, E8, E9, E10,
       FF_D1_p7, FF_D5_p4, FF_D6_p7, FF_D10_p4, FF_E1_p7, FF_E5_p4, FF_E6_p7, FF_E10_p4, GOL, M, or_1_out,
       or_2_out, or_3_out, or_4_out, or_5_out, or_6_out, or_7_out, or_8_out, or_9_out, or_10_out, or_11_out,
       or_12_out, or_13_out, undriven, undriven_2, undriven_3, undriven_4, undriven_5, undriven_6,
       undriven_7, undriven_8;

  Button Jog_1_E1_52d1f828 (.out(BE1));
  Button Jog_2_E2_46d6d327 (.out(BE2));
  Button Jog_3_E3_eee66431 (.out(BE3));
  Button Jog_4_E4_508ecdd4 (.out(BE4));
  Button Jog_5_E5_b167956b (.out(BE5));
  Button Jog_6_E6_6ecad8d6 (.out(BE6));
  Button Jog_7_E7_85017a97 (.out(BE7));
  Button Atacante_8_E8_2c360b22 (.out(BE8));
  Button Atacante_9_E9_4066b1cf (.out(BE9));
  Button Atacante_10_E10_e33676bd (.out(BE10));
  Button u_GOL (.out(B_GE));
  or or_1 (or_1_out, E8, D10);
  or or_2 (or_2_out, B_GE, B_GD);
  or or_3 (or_3_out, E1, E5);
  or or_4 (or_4_out, E6, E10);
  or or_5 (or_5_out, D1, D5);
  or or_6 (or_6_out, D6, D10);
  and and_1 (GOL, or_1_out, or_2_out);
  or or_7 (or_7_out, or_3_out, or_4_out);
  or or_8 (or_8_out, or_5_out, or_6_out);
  LED led_1 (.in(1'b1));
  LED led_2 (.in(E5));
  LED led_3 (.in(E7));
  // D_Flip_Flop FF_E1: pin names not known; wires that end beside it: CLK, BE1, CLK, BE2, E1, E2, FF_E1_p7
  D_Flip_Flop FF_E2 (.preset(FF_E1_p7), .reset(undriven));  // open: D, clk, Q, Qn
  D_Flip_Flop FF_E3 (.preset(undriven), .reset(undriven_2));  // open: D, clk, Q, Qn
  D_Flip_Flop FF_E4 (.preset(undriven_2), .reset(FF_E5_p4));  // open: D, clk, Q, Qn
  // D_Flip_Flop FF_E5: pin names not known; wires that end beside it: CLK, BE5, E5, FF_E5_p4
  or or_9 (or_9_out, or_7_out, or_8_out);
  LED led_4 (.in(E1));
  LED led_5 (.in(E2));
  LED led_6 (.in(E3));
  LED led_7 (.in(D9));
  LED led_8 (.in(E6));
  LED led_9 (.in(D10));
  not not_1 (M, or_9_out);
  LED led_10 (.in(D1));
  LED led_11 (.in(D4));
  LED led_12 (.in(E4));
  LED led_13 (.in(D8));
  // D_Flip_Flop FF_E6: pin names not known; wires that end beside it: CLK, BE6, CLK, BE7, E6, E7, FF_E6_p7
  D_Flip_Flop FF_E7 (.preset(FF_E6_p7), .reset(undriven_3));  // open: D, clk, Q, Qn
  D_Flip_Flop FF_E8 (.preset(undriven_3), .reset(undriven_4));  // open: D, clk, Q, Qn
  D_Flip_Flop FF_E9 (.preset(undriven_4), .reset(FF_E10_p4));  // open: D, clk, Q, Qn
  // D_Flip_Flop FF_E10: pin names not known; wires that end beside it: CLK, BE10, E10, FF_E10_p4
  or or_10 (or_10_out, BE1, BE5);
  or or_11 (or_11_out, BE6, BE10);
  or or_12 (or_12_out, BD1, BD5);
  or or_13 (or_13_out, BD6, BD10);
  LED led_14 (.in(D3));
  LED led_15 (.in(M));
  LED led_16 (.in(D6));
  LED led_17 (.in(E8));
  LED led_18 (.in(E9));
  LED led_19 (.in(E10));
  // D_Flip_Flop FF_D1: pin names not known; wires that end beside it: CLK, BD1, CLK, BD2, D1, D2, FF_D1_p7
  D_Flip_Flop FF_D2 (.preset(FF_D1_p7), .reset(undriven_5));  // open: D, clk, Q, Qn
  D_Flip_Flop FF_D3 (.preset(undriven_5), .reset(undriven_6));  // open: D, clk, Q, Qn
  D_Flip_Flop FF_D4 (.preset(undriven_6), .reset(FF_D5_p4));  // open: D, clk, Q, Qn
  // D_Flip_Flop FF_D5: pin names not known; wires that end beside it: CLK, BD5, D5, FF_D5_p4
  or or_14 (CLK, or_10_out, or_13_out);
  LED led_20 (.in(D2));
  LED led_21 (.in(D5));
  LED led_22 (.in(D7));
  LED led_23 (.in(1'b1));
  // D_Flip_Flop FF_D6: pin names not known; wires that end beside it: CLK, BD6, CLK, BD7, D6, D7, FF_D6_p7
  D_Flip_Flop FF_D7 (.preset(FF_D6_p7), .reset(undriven_7));  // open: D, clk, Q, Qn
  D_Flip_Flop FF_D8 (.preset(undriven_7), .reset(undriven_8));  // open: D, clk, Q, Qn
  D_Flip_Flop FF_D9 (.preset(undriven_8), .reset(FF_D10_p4));  // open: D, clk, Q, Qn
  // D_Flip_Flop FF_D10: pin names not known; wires that end beside it: CLK, BD10, D10, FF_D10_p4
  Button Jog_1_D1_d13047cd (.out(BD1));
  Button Jog_2_D2_b1320820 (.out(BD2));
  Button Jog_3_D3_2af111aa (.out(BD3));
  Button Jog_4_D4_25b4507c (.out(BD4));
  Button Jog_5_D5_fbed1a54 (.out(BD5));
  Button Jog_6_D6_fac2830b (.out(BD6));
  Button Jog_7_D7_05766550 (.out(BD7));
  Button Jog_8_D8_9ff1dcc2 (.out(BD8));
  Button Atacante_9_D9_e0273248 (.out(BD9));
  Button Atacante_10_D10_9c6eb609 (.out(BD10));
  Button button_1 (.out(B_GD));

  // Notes on the sheet:
  //   Time Esquerda
  //   VALIDADOR DE GOL
  //   CONTROLE DO LED AMARELO CENTRAL
  //   GERADOR DE PULSO DE ATUALIZAÇÃO
  //   CIRCUITO DE CONTROLE DE POSSE DE BOLA E VALIDACAO DE GOL
  //   Time Direita
endmodule

module Placar (
);

  wire counter_1_carry, counter_3_carry, Gol_ASA_out, Gol_Visitante_out, reset_ASA_out, reset_Visitante_out;
  wire [3:0] counter_1_q, counter_2_q, counter_3_q, counter_4_q;

  Button Gol_ASA (.out(Gol_ASA_out));
  Button reset_ASA (.out(reset_ASA_out));
  Counter #(.max('h9), .width(4)) counter_1 (
    .count(Gol_ASA_out), .Q(counter_1_q), .carry(counter_1_carry), .clk(Gol_ASA_out), .clr(reset_ASA_out));  // open: load, D, up
  Counter #(.max('h9), .width(4)) counter_2 (
    .count(counter_1_carry), .Q(counter_2_q), .clk(Gol_ASA_out), .clr(reset_ASA_out));  // open: load, D, carry, up
  Hex_Digit_Display hex_digit_display_1 (.value(counter_2_q));  // open: dp
  Hex_Digit_Display hex_digit_display_2 (.value(counter_1_q));  // open: dp
  Hex_Digit_Display hex_digit_display_3 (.value(counter_4_q));  // open: dp
  Hex_Digit_Display hex_digit_display_4 (.value(counter_3_q));  // open: dp
  Counter #(.max('h9), .width(4)) counter_3 (
    .count(Gol_Visitante_out), .Q(counter_3_q), .carry(counter_3_carry), .clk(Gol_Visitante_out),
    .clr(reset_Visitante_out));  // open: load, D, up
  Counter #(.max('h9), .width(4)) counter_4 (
    .count(counter_3_carry), .Q(counter_4_q), .clk(Gol_Visitante_out), .clr(reset_Visitante_out));  // open: load, D, carry, up
  Button Gol_Visitante (.out(Gol_Visitante_out));
  Button reset_Visitante (.out(reset_Visitante_out));
endmodule

module Cronometro (
  input  Run
);

  wire and_1_out, and_2_out, and_3_out, clock_1_out, De_Seg_carry, Reset_out, Uni_min_carry, Uni_seg_carry;
  wire [3:0] De_min_q, De_Seg_q, Uni_min_q, Uni_seg_q;

  Clock clock_1 (.out(clock_1_out));
  and and_1 (and_1_out, Run, clock_1_out);
  Button Reset (.out(Reset_out));
  Counter #(.max('h9), .width(4)) Uni_min (
    .count(and_3_out), .Q(Uni_min_q), .carry(Uni_min_carry), .clk(and_1_out), .clr(Reset_out));  // open: load, D, up
  and and_2 (and_2_out, Uni_min_carry, and_3_out);
  Counter #(.max('h9), .width(4)) De_min (
    .count(and_2_out), .Q(De_min_q), .clk(and_1_out), .clr(Reset_out));  // open: load, D, carry, up
  Hex_Digit_Display hex_digit_display_1 (.value(De_min_q));  // open: dp
  Hex_Digit_Display hex_digit_display_2 (.value(Uni_min_q));  // open: dp
  Hex_Digit_Display hex_digit_display_3 (.value(De_Seg_q));  // open: dp
  Counter #(.max('h5), .width(4)) De_Seg (
    .count(Uni_seg_carry), .Q(De_Seg_q), .carry(De_Seg_carry), .clk(and_1_out), .clr(Reset_out));  // open: load, D, up
  Counter #(.max('h9), .width(4)) Uni_seg (
    .count(and_1_out), .Q(Uni_seg_q), .carry(Uni_seg_carry), .clk(and_1_out), .clr(Reset_out));  // open: load, D, up
  and and_3 (and_3_out, De_Seg_carry, Uni_seg_carry);
  Hex_Digit_Display hex_digit_display_4 (.value(Uni_seg_q));  // open: dp
endmodule
