// Logisim project sistema_substituicao.circ as structural Verilog: 1 circuit, main circuit main
module main (
  input  [3:0] SAI_DEZENA,
  input  [3:0] SAI_UNIDADE,
  input  [3:0] ENTRA_DEZENA,
  input  [3:0] ENTRA_UNIDADE
);

  wire and_1_out, and_2_out, clock_1_out, comparator_1_eq, comparator_2_eq, CONFIRMAR_out, not_1_out,
       RESET_out;
  wire [3:0] \CONT_SUBSTITUIÇOES_q , REG_ENTRA_DEZENA_q, REG_ENTRA_UNIDADE_q, REG_SAI_DEZENA_q,
       REG_SAI_UNIDADE_q;

  Clock clock_1 (.out(clock_1_out));
  Button CONFIRMAR (.out(CONFIRMAR_out));
  Button RESET (.out(RESET_out));
  Comparator #(.width(4), .mode("unsigned")) comparator_1 (
    .a(SAI_DEZENA), .b(ENTRA_DEZENA), .eq(comparator_1_eq));  // open: gt, lt
  Comparator #(.width(4), .mode("unsigned")) comparator_2 (
    .a(SAI_UNIDADE), .b(ENTRA_UNIDADE), .eq(comparator_2_eq));  // open: gt, lt
  Register #(.width(4)) REG_SAI_DEZENA (
    .D(SAI_DEZENA), .en(and_2_out), .Q(REG_SAI_DEZENA_q), .clk(clock_1_out), .clr(RESET_out));
  Register #(.width(4)) REG_SAI_UNIDADE (
    .D(SAI_UNIDADE), .en(and_2_out), .Q(REG_SAI_UNIDADE_q), .clk(clock_1_out), .clr(RESET_out));
  Register #(.width(4)) REG_ENTRA_DEZENA (
    .D(ENTRA_DEZENA), .en(and_2_out), .Q(REG_ENTRA_DEZENA_q), .clk(clock_1_out), .clr(RESET_out));
  Register #(.width(4)) REG_ENTRA_UNIDADE (
    .D(ENTRA_UNIDADE), .en(and_2_out), .Q(REG_ENTRA_UNIDADE_q), .clk(clock_1_out), .clr(RESET_out));
  Counter #(.width(4), .max('hf), .ongoal("stay")) \CONT_SUBSTITUIÇOES  (
    .count(and_2_out), .Q(\CONT_SUBSTITUIÇOES_q ), .clk(clock_1_out), .clr(RESET_out));  // open: load, D, carry
  Hex_Digit_Display hex_digit_display_1 (.value(REG_SAI_DEZENA_q));  // open: dp
  Hex_Digit_Display hex_digit_display_2 (.value(REG_ENTRA_DEZENA_q));  // open: dp
  Hex_Digit_Display hex_digit_display_3 (.value(\CONT_SUBSTITUIÇOES_q ));  // open: dp
  and and_1 (and_1_out, comparator_1_eq, comparator_2_eq);
  Hex_Digit_Display hex_digit_display_4 (.value(REG_SAI_UNIDADE_q));  // open: dp
  Hex_Digit_Display hex_digit_display_5 (.value(REG_ENTRA_UNIDADE_q));  // open: dp
  not not_1 (not_1_out, and_1_out);
  and and_2 (and_2_out, not_1_out, CONFIRMAR_out);
  LED led_1 (.in(and_2_out));
endmodule
